// Logisim project Main bus.circ as structural Verilog: 1 circuit, main circuit Main bus
module Main_bus (
  input  _1,
  input  _5,
  input  _10,
  input  _2,
  input  _3,
  input  _6,
  input  in_7,
  input  _7,
  input  _4,
  input  _8,
  input  _9,
  input  [15:0] in_12
);

  wire and_1_out;
  wire [2:0] counter_1_q;
  wire [15:0] Accumulator_register_q, controlled_buffer_1_out, controlled_buffer_3_out,
       controlled_buffer_5_out, controlled_buffer_6_out, controlled_buffer_7_out, controlled_buffer_8_out,
       Input_register_2_q, Input_register_q, Instruction_register_q, Memory_access_register_q,
       Output_register_q, Program_counter_q, ram_1_data, undriven;

  Register #(.width(16)) Memory_access_register (
    .D(controlled_buffer_3_out), .en(1'b1), .Q(Memory_access_register_q), .clk(in_7));  // open: clr
  Register #(.width(16)) Instruction_register (
    .D(controlled_buffer_7_out), .en(1'b1), .Q(Instruction_register_q), .clk(in_7));  // open: clr
  Counter #(.width(3), .max('h7)) counter_1 (
    .count(1'b1), .Q(counter_1_q), .clk(in_7), .clr(and_1_out));  // open: load, D, carry
  and and_1 (and_1_out, counter_1_q[2], counter_1_q[1], counter_1_q[0]);
  Counter #(.width(16), .max('hffff)) Program_counter (
    .count(_10), .Q(Program_counter_q), .clk(in_7));  // open: load, D, carry, clr
  RAM #(.addrWidth(16), .dataWidth(16)) ram_1 (
    .addr(Memory_access_register_q), .data(ram_1_data), .clk(in_7), .ld(1'b1));  // open: sel, clr
  ROM #(.addrWidth(4), .dataWidth(16)) rom_1 (.addr(Instruction_register_q[3:0]));  // open: data, sel
  assign controlled_buffer_1_out = _1 ? Program_counter_q : 16'bz;  // Controlled_Buffer controlled_buffer_1
  assign controlled_buffer_1_out = _5 ? Accumulator_register_q : 16'bz;  // Controlled_Buffer controlled_buffer_2
  assign controlled_buffer_3_out = _2 ? controlled_buffer_1_out : 16'bz;  // Controlled_Buffer controlled_buffer_3
  assign controlled_buffer_1_out = _3 ? ram_1_data : 16'bz;  // Controlled_Buffer controlled_buffer_4
  assign controlled_buffer_5_out = _6 ? controlled_buffer_1_out : 16'bz;  // Controlled_Buffer controlled_buffer_5
  assign controlled_buffer_6_out = _7 ? controlled_buffer_1_out : 16'bz;  // Controlled_Buffer controlled_buffer_6
  assign controlled_buffer_7_out = _4 ? controlled_buffer_1_out : 16'bz;  // Controlled_Buffer controlled_buffer_7
  assign controlled_buffer_8_out = _8 ? controlled_buffer_1_out : 16'bz;  // Controlled_Buffer controlled_buffer_8
  assign controlled_buffer_1_out = _9 ? in_12 : 16'bz;  // Controlled_Buffer controlled_buffer_9
  Register #(.width(16)) Output_register (
    .D(controlled_buffer_8_out), .Q(Output_register_q), .clk(in_7));  // open: en, clr
  Register #(.width(16)) Input_register (
    .D(controlled_buffer_5_out), .en(1'b1), .Q(Input_register_q), .clk(in_7));  // open: clr
  Register #(.width(16)) Input_register_2 (
    .D(controlled_buffer_6_out), .en(1'b1), .Q(Input_register_2_q), .clk(in_7));  // open: clr
  Hex_Digit_Display hex_digit_display_1 (.value(Output_register_q[15:12]));  // open: dp
  Hex_Digit_Display hex_digit_display_2 (.value(Output_register_q[7:4]));  // open: dp
  Hex_Digit_Display hex_digit_display_3 (.value(Output_register_q[11:8]));  // open: dp
  Register #(.width(16)) Accumulator_register (
    .D(undriven), .en(1'b1), .Q(Accumulator_register_q), .clr(in_7));  // open: clk
  Hex_Digit_Display hex_digit_display_4 (.value(Output_register_q[3:0]));  // open: dp

  // Other names for the same wires on the sheet: clk = in_7

  // Notes on the sheet:
  //   ROM for control matrix
  //   ALU
endmodule
